// Logisim project a.circ as structural Verilog: 1 circuit, main circuit main
module main (
  input  x,
  input  y,
  output XOR_y
);

  wire And1_out, And2_out, not_1_out, not_2_out;

  not not_1 (not_1_out, y);
  not not_2 (not_2_out, x);
  and And1 (And1_out, x, not_1_out);
  and And2 (And2_out, not_2_out, y);
  or OR1 (XOR_y, And1_out, And2_out);
endmodule
