// Logisim project decoder_library.circ as structural Verilog: 20 circuits, main circuit Decoder_2_4
module Decoder_2_4 (
  input  In_0,
  input  In_1,
  output Out_0,
  output Out_1,
  output Out_2,
  output Out_3
);

  wire not_1_out, not_2_out;

  not not_1 (not_1_out, In_1);
  not not_2 (not_2_out, In_0);
  and and_1 (Out_0, not_2_out, not_1_out);
  and and_2 (Out_1, not_2_out, In_1);
  and and_3 (Out_2, In_0, not_1_out);
  and and_4 (Out_3, In_0, In_1);
endmodule

module Decoder_3_8 (
  input  In_0,
  input  In_1,
  input  In_2,
  output [7:0] out_4
);

  wire decoder_2_4_1_out_0, decoder_2_4_1_out_1, decoder_2_4_1_out_2, decoder_2_4_1_out_3, not_1_out;

  not not_1 (not_1_out, In_0);
  Decoder_2_4 decoder_2_4_1 (
    .In_0(In_1), .In_1(In_2), .Out_0(decoder_2_4_1_out_0), .Out_1(decoder_2_4_1_out_1),
    .Out_2(decoder_2_4_1_out_2), .Out_3(decoder_2_4_1_out_3));
  and and_1 (out_4[0], not_1_out, decoder_2_4_1_out_0);
  and and_2 (out_4[1], not_1_out, decoder_2_4_1_out_1);
  and and_3 (out_4[2], not_1_out, decoder_2_4_1_out_2);
  and and_4 (out_4[3], not_1_out, decoder_2_4_1_out_3);
  and and_5 (out_4[4], In_0, decoder_2_4_1_out_0);
  and and_6 (out_4[5], decoder_2_4_1_out_1, In_0);
  and and_7 (out_4[6], decoder_2_4_1_out_2, In_0);
  and and_8 (out_4[7], decoder_2_4_1_out_3, In_0);
endmodule

module Decoder_7_LED (
  input  in_1,
  input  in_2
);

  wire clock_1_out, decoder_2_4_1_out_0, decoder_2_4_1_out_1, decoder_2_4_1_out_2, decoder_2_4_1_out_3,
       decoder_2_4_2_out_0, decoder_2_4_2_out_1, decoder_2_4_2_out_2, decoder_2_4_2_out_3;
  wire [3:0] adder_4_1_out_0, b_1_out0, dipswitch_1_sw4, dipswitch_2_sw4, dipswitch_3_sw4;
  wire [7:0] or_1_out, undriven, undriven_2, undriven_3, undriven_4, undriven_5, undriven_6, undriven_7,
       undriven_8, undriven_9, undriven_10, undriven_11, undriven_12, undriven_13, undriven_14, undriven_15,
       undriven_16;
  wire [15:0] dipswitch_4_sw16;

  DipSwitch #(.number(4)) dipswitch_1 (
    .sw1(dipswitch_1_sw4[3]), .sw2(dipswitch_1_sw4[2]), .sw3(dipswitch_1_sw4[1]), .sw4(dipswitch_1_sw4[0]));
  DipSwitch #(.number(4)) dipswitch_2 (
    .sw1(dipswitch_2_sw4[3]), .sw2(dipswitch_2_sw4[2]), .sw3(dipswitch_2_sw4[1]), .sw4(dipswitch_2_sw4[0]));
  DipSwitch #(.number(4)) dipswitch_3 (
    .sw1(dipswitch_3_sw4[3]), .sw2(dipswitch_3_sw4[2]), .sw3(dipswitch_3_sw4[1]), .sw4(dipswitch_3_sw4[0]));
  DipSwitch #(.number(16)) dipswitch_4 (
    .sw1(dipswitch_4_sw16[15]), .sw2(dipswitch_4_sw16[14]), .sw3(dipswitch_4_sw16[13]),
    .sw4(dipswitch_4_sw16[12]), .sw5(dipswitch_4_sw16[11]), .sw6(dipswitch_4_sw16[10]),
    .sw7(dipswitch_4_sw16[9]), .sw8(dipswitch_4_sw16[8]), .sw9(dipswitch_4_sw16[7]),
    .sw10(dipswitch_4_sw16[6]), .sw11(dipswitch_4_sw16[5]), .sw12(dipswitch_4_sw16[4]),
    .sw13(dipswitch_4_sw16[3]), .sw14(dipswitch_4_sw16[2]), .sw15(dipswitch_4_sw16[1]),
    .sw16(dipswitch_4_sw16[0]));
  Encode16_4 encode16_4_1 (.in_1(dipswitch_4_sw16));  // open: out_2
  b b_1 (.In0(dipswitch_3_sw4), .Reset(in_1), .Enable(in_2), .Clock(clock_1_out), .Out0(b_1_out0));
  Clock clock_1 (.out(clock_1_out));
  Adder_4 adder_4_1 (
    .In0_4(dipswitch_1_sw4), .In1_4(dipswitch_2_sw4), .Out_0(adder_4_1_out_0));  // open: Cin_0, Carry_0
  Decoder_2_4 decoder_2_4_1 (
    .In_0(b_1_out0[0]), .In_1(b_1_out0[1]), .Out_0(decoder_2_4_1_out_0), .Out_1(decoder_2_4_1_out_1),
    .Out_2(decoder_2_4_1_out_2), .Out_3(decoder_2_4_1_out_3));
  Decoder_2_4 decoder_2_4_2 (
    .In_0(b_1_out0[2]), .In_1(b_1_out0[3]), .Out_0(decoder_2_4_2_out_0), .Out_1(decoder_2_4_2_out_1),
    .Out_2(decoder_2_4_2_out_2), .Out_3(decoder_2_4_2_out_3));
  and and_1 (undriven_2[7], decoder_2_4_1_out_0, decoder_2_4_2_out_0);
  and and_2 (undriven_3[6], decoder_2_4_2_out_0, decoder_2_4_1_out_2);
  and and_3 (undriven_4[7], decoder_2_4_1_out_1, decoder_2_4_2_out_0);
  and and_4 (undriven_5[7], decoder_2_4_1_out_3, decoder_2_4_2_out_0);
  and and_5 (undriven_6[6], decoder_2_4_2_out_2, decoder_2_4_1_out_0);
  and and_6 (undriven_9[7], decoder_2_4_1_out_2, decoder_2_4_2_out_2);
  and and_7 (undriven_7[7], decoder_2_4_1_out_1, decoder_2_4_2_out_2);
  and and_8 (undriven_10[7], decoder_2_4_1_out_3, decoder_2_4_2_out_2);
  and and_9 (undriven_11[7], decoder_2_4_1_out_0, decoder_2_4_2_out_1);
  and and_10 (undriven_12[7], decoder_2_4_1_out_2, decoder_2_4_2_out_1);
  and and_11 (undriven[7], decoder_2_4_1_out_1, decoder_2_4_2_out_1);
  and and_12 (undriven_8[5], decoder_2_4_1_out_3, decoder_2_4_2_out_1);
  and and_13 (undriven_13[7], decoder_2_4_1_out_0, decoder_2_4_2_out_3);
  and and_14 (undriven_14[6], decoder_2_4_1_out_2, decoder_2_4_2_out_3);
  and and_15 (undriven_15[7], decoder_2_4_1_out_1, decoder_2_4_2_out_3);
  and and_16 (undriven_16[7], decoder_2_4_1_out_3, decoder_2_4_2_out_3);
  assign or_1_out = {{6{undriven_2[7]}}, undriven_2[1:0]} | {undriven_3[7:6], undriven_3[6], undriven_3[4:0]} | {{2{undriven_4[7]}}, undriven_4[5], {2{undriven_4[7]}}, undriven_4[2], undriven_4[7], undriven_4[0]} | {{4{undriven_5[7]}}, undriven_5[3:2], undriven_5[7], undriven_5[0]} | {undriven_6[7:6], undriven_6[6], undriven_6[4:3], {2{undriven_6[6]}}, undriven_6[0]} | {undriven_9[7:6], {2{undriven_9[7]}}, undriven_9[3], {2{undriven_9[7]}}, undriven_9[0]} | {undriven_7[7:6], {5{undriven_7[7]}}, undriven_7[0]} | {{3{undriven_10[7]}}, undriven_10[4:0]} | {{7{undriven_11[7]}}, undriven_11[0]} | {{4{undriven_12[7]}}, undriven_12[3], {2{undriven_12[7]}}, undriven_12[0]} | {{3{undriven[7]}}, undriven[4], {3{undriven[7]}}, undriven[0]} | {undriven_8[7:5], {4{undriven_8[5]}}, undriven_8[0]} | {undriven_13[7:5], {3{undriven_13[7]}}, undriven_13[1:0]} | {undriven_14[7:6], {3{undriven_14[6]}}, undriven_14[2], undriven_14[6], undriven_14[0]} | {undriven_15[7:5], {4{undriven_15[7]}}, undriven_15[0]} | {undriven_16[7:4], {3{undriven_16[7]}}, undriven_16[0]};  // OR_Gate or_1, 8 bits wide
  _7_Segment_Display u_7_segment_display_1 (
    .g(or_1_out[1]), .f(or_1_out[2]), .a(or_1_out[7]), .b(or_1_out[6]), .e(or_1_out[3]), .d(or_1_out[4]),
    .c(or_1_out[5]), .dp(or_1_out[0]));
endmodule

module Encode16_4 (
  input  [15:0] in_1,
  output [3:0] out_2
);

  or or_1 (out_2[0], in_1[14], in_1[12], in_1[10], in_1[8], in_1[6], in_1[4], in_1[2], in_1[0]);
  or or_2 (out_2[1], in_1[13], in_1[12], in_1[9], in_1[8], in_1[5], in_1[4], in_1[1], in_1[0]);
  or or_3 (out_2[2], in_1[11], in_1[10], in_1[9], in_1[8], in_1[3], in_1[2], in_1[1], in_1[0]);
  or or_4 (out_2[3], in_1[7], in_1[6], in_1[5], in_1[4], in_1[3], in_1[2], in_1[1], in_1[0]);
endmodule

module Encode4_2_Fri (
  input  [3:0] in_1,
  output [1:0] out_2
);

  wire and_1_out, not_1_out, or_1_out;

  not not_1 (not_1_out, in_1[3]);
  or or_1 (or_1_out, in_1[3], in_1[1]);
  or or_2 (out_2[1], in_1[3], in_1[2]);
  and and_1 (and_1_out, in_1[1], not_1_out, in_1[2]);
  xor xor_1 (out_2[0], or_1_out, and_1_out);
endmodule

module Mux_2_1 (
  input  Sel0,
  input  In0,
  input  In1,
  output Out0
);

  wire and_1_out, and_2_out, not_1_out;

  not not_1 (not_1_out, Sel0);
  and and_1 (and_1_out, In0, not_1_out);
  and and_2 (and_2_out, Sel0, In1);
  or or_1 (Out0, and_1_out, and_2_out);
endmodule

module Mux_4_1 (
  input  [1:0] Sel0,
  input  [2:0] In0,
  input  [2:0] In1,
  input  [2:0] In2,
  input  [2:0] In3,
  output [2:0] Out0
);

  wire [2:0] and_1_out, and_2_out, and_3_out, and_4_out;
  wire [2:2] decoder_2_4_1_out_0, decoder_2_4_1_out_1, decoder_2_4_1_out_2, decoder_2_4_1_out_3;

  Decoder_2_4 decoder_2_4_1 (
    .In_0(Sel0[0]), .In_1(Sel0[1]), .Out_0(decoder_2_4_1_out_0[2]), .Out_1(decoder_2_4_1_out_1[2]),
    .Out_2(decoder_2_4_1_out_2[2]), .Out_3(decoder_2_4_1_out_3[2]));
  assign and_1_out = In0 & {3{decoder_2_4_1_out_0[2]}};  // AND_Gate and_1, 3 bits wide
  assign and_2_out = In1 & {3{decoder_2_4_1_out_2[2]}};  // AND_Gate and_2, 3 bits wide
  assign and_3_out = In2 & {3{decoder_2_4_1_out_1[2]}};  // AND_Gate and_3, 3 bits wide
  assign and_4_out = In3 & {3{decoder_2_4_1_out_3[2]}};  // AND_Gate and_4, 3 bits wide
  assign Out0 = and_1_out | and_2_out | and_3_out | and_4_out;  // OR_Gate or_1, 3 bits wide
endmodule

module Compar_4_1 (
  input  [3:0] In0,
  input  [3:0] In1,
  output Out0
);

  wire xnor_1_out, xnor_2_out, xnor_3_out, xnor_4_out;

  xnor xnor_1 (xnor_1_out, In1[0], In0[0]);
  xnor xnor_2 (xnor_2_out, In1[1], In0[1]);
  xnor xnor_3 (xnor_3_out, In1[2], In0[2]);
  xnor xnor_4 (xnor_4_out, In1[3], In0[3]);
  and and_1 (Out0, xnor_1_out, xnor_2_out, xnor_3_out, xnor_4_out);
endmodule

module test (
  input  in_1,
  input  in_2,
  input  in_3,
  input  in_4
);

  wire compar_4_1_1_out0, d_flip_reset_1_out_4, d_latch_rest_1_out_5, d_latch_rest_1_q, not_1_out, not_2_out,
       undriven;
  wire [3:0] dipswitch_1_sw4, dipswitch_2_sw4;

  DipSwitch #(.number(4)) dipswitch_1 (
    .sw1(dipswitch_1_sw4[3]), .sw2(dipswitch_1_sw4[2]), .sw3(dipswitch_1_sw4[1]), .sw4(dipswitch_1_sw4[0]));
  DipSwitch #(.number(4)) dipswitch_2 (
    .sw1(dipswitch_2_sw4[3]), .sw2(dipswitch_2_sw4[2]), .sw3(dipswitch_2_sw4[1]), .sw4(dipswitch_2_sw4[0]));
  Compar_4_1 compar_4_1_1 (.In0(dipswitch_1_sw4), .In1(dipswitch_2_sw4), .Out0(compar_4_1_1_out0));
  D_latch_Rest d_latch_rest_1 (
    .D(undriven), .Rest(in_1), .We(in_3), .Q(d_latch_rest_1_q), .out_5(d_latch_rest_1_out_5));
  not not_1 (not_1_out, d_latch_rest_1_out_5);
  LED led_1 (.in(compar_4_1_1_out0));
  D_Flip_Reset d_flip_reset_1 (.Reset(not_2_out), .D(in_2), .Clock(in_4), .out_4(d_flip_reset_1_out_4));
  not not_2 (not_2_out, d_flip_reset_1_out_4);
endmodule

module halfadd_1 (
  input  In0,
  input  In1,
  output Carry0,
  output Sum0
);

  and and_1 (Carry0, In0, In1);
  xor xor_1 (Sum0, In0, In1);
endmodule

module fulladd_1 (
  input  In0,
  input  In1,
  input  In2,
  output Carry0,
  output Sum0
);

  wire halfadd_1_1_carry0, halfadd_1_1_sum0, halfadd_1_2_carry0;

  halfadd_1 halfadd_1_1 (.In0(In0), .In1(In1), .Carry0(halfadd_1_1_carry0), .Sum0(halfadd_1_1_sum0));
  halfadd_1 halfadd_1_2 (.In0(halfadd_1_1_sum0), .In1(In2), .Carry0(halfadd_1_2_carry0), .Sum0(Sum0));
  or or_1 (Carry0, halfadd_1_1_carry0, halfadd_1_2_carry0);
endmodule

module Adder_4 (
  input  Cin_0,
  input  [3:0] In0_4,
  input  [3:0] In1_4,
  output Carry_0,
  output [3:0] Out_0
);

  wire fulladd_1_1_carry0, fulladd_1_2_carry0, fulladd_1_3_carry0;

  fulladd_1 fulladd_1_1 (.In0(Cin_0), .In1(In0_4[0]), .In2(In1_4[0]), .Carry0(fulladd_1_1_carry0), .Sum0(Out_0[0]));
  fulladd_1 fulladd_1_2 (
    .In0(fulladd_1_1_carry0), .In1(In0_4[1]), .In2(In1_4[1]), .Carry0(fulladd_1_2_carry0), .Sum0(Out_0[1]));
  fulladd_1 fulladd_1_3 (
    .In0(fulladd_1_2_carry0), .In1(In0_4[2]), .In2(In1_4[2]), .Carry0(fulladd_1_3_carry0), .Sum0(Out_0[2]));
  fulladd_1 fulladd_1_4 (.In0(fulladd_1_3_carry0), .In1(In0_4[3]), .In2(In1_4[3]), .Carry0(Carry_0), .Sum0(Out_0[3]));
endmodule

module SRLatch (
  input  S,
  input  R,
  input  in_3,
  input  in_4,
  output Qf,
  output Q,
  output out_7,
  output out_8
);

  nor nor_1 (Q, Qf, R);
  nand nand_1 (out_7, in_3, out_8);
  nand nand_2 (out_8, out_7, in_4);
  nor nor_2 (Qf, S, Q);
endmodule

module D_Latch (
  input  D,
  input  We,
  output Q,
  output Qf
);

  wire and_1_out, and_2_out, not_1_out;

  not not_1 (not_1_out, D);
  and and_1 (and_1_out, D, We);
  and and_2 (and_2_out, We, not_1_out);
  nor nor_1 (Qf, and_1_out, Q);
  nor nor_2 (Q, Qf, and_2_out);
endmodule

module D_latch_Rest (
  input  D,
  input  Rest,
  input  We,
  output Q,
  output out_5
);

  wire and_1_out, nor_1_out, nor_2_out, not_1_out;

  and and_1 (and_1_out, D, We);
  not not_1 (not_1_out, and_1_out);
  nor nor_1 (nor_1_out, and_1_out, nor_2_out);
  nor nor_2 (nor_2_out, not_1_out, nor_1_out);
  Mux_2_1 mux_2_1_1 (.Sel0(Rest), .In0(nor_2_out), .Out0(Q));  // open: In1
endmodule

module DFlipFlop (
  input  D,
  input  Clock,
  output Q
);

  wire d_latch_1_q, not_1_out;

  not not_1 (not_1_out, Clock);
  D_Latch d_latch_1 (.D(D), .We(not_1_out), .Q(d_latch_1_q));  // open: Qf
  D_Latch d_latch_2 (.D(d_latch_1_q), .We(Clock), .Q(Q));  // open: Qf
endmodule

module D_Flip_Reset (
  input  Reset,
  input  D,
  input  Clock,
  output out_4
);

  wire and_1_out;

  and and_1 (and_1_out, Reset, D);
  DFlipFlop dflipflop_1 (.D(and_1_out), .Clock(Clock), .Q(out_4));
endmodule

module DFlipE (
  input  D,
  input  En,
  input  Clock,
  output Q
);

  wire and_1_out, d_latch_1_q, not_1_out;

  and and_1 (and_1_out, D, En);
  not not_1 (not_1_out, Clock);
  D_Latch d_latch_1 (.D(and_1_out), .We(not_1_out), .Q(d_latch_1_q));  // open: Qf
  D_Latch d_latch_2 (.D(d_latch_1_q), .We(Clock), .Q(Q));  // open: Qf
endmodule

module a (
  input  [3:0] In0,
  input  En,
  input  Clock,
  output [3:0] Out0
);

  DFlipE dflipe_1 (.D(In0[3]), .En(En), .Clock(Clock), .Q(Out0[3]));
  DFlipE dflipe_2 (.D(In0[2]), .En(En), .Clock(Clock), .Q(Out0[2]));
  DFlipE dflipe_3 (.D(In0[1]), .En(En), .Clock(Clock), .Q(Out0[1]));
  DFlipE dflipe_4 (.D(In0[0]), .En(En), .Clock(Clock), .Q(Out0[0]));
endmodule

module b (
  input  [3:0] In0,
  input  Reset,
  input  Enable,
  input  Clock,
  output [3:0] Out0
);

  wire and_1_out, and_2_out, and_3_out, and_4_out, not_1_out;

  and and_1 (and_1_out, In0[3], Enable);
  not not_1 (not_1_out, Reset);
  D_Flip_Reset d_flip_reset_1 (.Reset(not_1_out), .D(and_1_out), .Clock(Clock), .out_4(Out0[3]));
  and and_2 (and_2_out, In0[2], Enable);
  D_Flip_Reset d_flip_reset_2 (.Reset(not_1_out), .D(and_2_out), .Clock(Clock), .out_4(Out0[2]));
  and and_3 (and_3_out, In0[1], Enable);
  D_Flip_Reset d_flip_reset_3 (.Reset(not_1_out), .D(and_3_out), .Clock(Clock), .out_4(Out0[1]));
  and and_4 (and_4_out, In0[0], Enable);
  D_Flip_Reset d_flip_reset_4 (.Reset(not_1_out), .D(and_4_out), .Clock(Clock), .out_4(Out0[0]));
endmodule
